// Logisim project 16bit_risc_cpu.circ as structural Verilog: 5 circuits, main circuit main
module main (
);

  wire alu_1_c, alu_1_n, alu_1_v, clock_1_out, controlunit_1_alusrc, controlunit_1_branch,
       controlunit_1_jump, controlunit_1_memread, controlunit_1_memtoreg, controlunit_1_memwrite,
       controlunit_1_regwrite;
  wire [2:0] controlunit_1_aluop;
  wire [11:0] rom_1_data;
  wire [15:0] adder_1_out, alu_1_result, bit_extender_1_out, bit_extender_2_out, multiplexer_1_out,
       multiplexer_2_out, multiplexer_3_out, pc_1_pc_out, registerfile_1_rs1_data, registerfile_1_rs2_data;
  wire [15:12] rom_1_data_2;

  Multiplexer #(.width(16)) multiplexer_1 (
    .in0(16'h1), .in1(bit_extender_2_out), .out(multiplexer_1_out), .sel(controlunit_1_branch));
  Adder #(.width(16)) adder_1 (.a(pc_1_pc_out), .b(multiplexer_1_out), .out(adder_1_out));  // open: cin, cout
  ROM #(.addrWidth(16), .dataWidth(16)) rom_1 (.addr(pc_1_pc_out), .data({rom_1_data_2, rom_1_data}));
  PC pc_1 (
    .BranchTarget(adder_1_out), .jumptarget(bit_extender_1_out), .jump(controlunit_1_jump), .reset(1'b0),
    .branch(controlunit_1_branch), .PC_out(pc_1_pc_out));
  assign bit_extender_1_out = {{4{1'b0}}, rom_1_data};  // Bit_Extender bit_extender_1
  Clock clock_1 (.out(clock_1_out));
  assign bit_extender_2_out = {{12{rom_1_data[3]}}, rom_1_data[3:0]};  // Bit_Extender bit_extender_2
  Multiplexer #(.width(16)) multiplexer_2 (
    .in0(registerfile_1_rs2_data), .in1(bit_extender_2_out), .out(multiplexer_2_out),
    .sel(controlunit_1_alusrc));
  RegisterFile registerfile_1 (
    .Rs2_Addr(rom_1_data[3:0]), .Rs1_Addr(rom_1_data[7:4]), .Write_data(multiplexer_3_out),
    .clk(clock_1_out), .Reg_write(controlunit_1_regwrite), .Rd_addr(rom_1_data[11:8]),
    .Rs2_data(registerfile_1_rs2_data), .Rs1_Data(registerfile_1_rs1_data));
  ALU alu_1 (
    .A(registerfile_1_rs1_data), .B(multiplexer_2_out), .Op(controlunit_1_aluop), .Result(alu_1_result),
    .N(alu_1_n), .C(alu_1_c), .V(alu_1_v));
  RAM #(.addrWidth(16), .asyncread("true"), .dataWidth(16)) ram_1 (
    .addr(alu_1_result), .we(controlunit_1_memwrite), .oe(controlunit_1_memread), .clk(clock_1_out),
    .din(registerfile_1_rs2_data), .dout(registerfile_1_rs2_data));
  Multiplexer #(.width(16)) multiplexer_3 (
    .in0(alu_1_result), .in1(registerfile_1_rs2_data), .out(multiplexer_3_out), .sel(controlunit_1_memtoreg));
  // Probe on rom_1_data_2
  ControlUnit controlunit_1 (
    .Opcode(rom_1_data_2), .RegWrite(controlunit_1_regwrite), .MemRead(controlunit_1_memread),
    .MemWrite(controlunit_1_memwrite), .ALUSrc(controlunit_1_alusrc), .MemToReg(controlunit_1_memtoreg),
    .Branch(controlunit_1_branch), .Jump(controlunit_1_jump), .ALUOp(controlunit_1_aluop));

  // Notes on the sheet:
  //   contents of rom_1 (hex, n*v repeats v):
  //   1234 5678 9abc def0 1111 2222 3333 4444
endmodule

module ALU (
  input  [15:0] A,
  input  [15:0] B,
  input  [2:0] Op,
  output [15:0] Result,
  output N,
  output C,
  output V
);

  wire adder_1_cout, adder_2_cout, nor_1_out;
  wire [14:0] undriven;
  wire [15:0] adder_1_out, adder_2_out, and_1_out, not_1_out, or_1_out, shifter_1_out, shifter_2_out,
       shifter_3_out, xor_1_out;

  assign not_1_out = ~B;  // NOT_Gate not_1, 16 bits wide
  Adder #(.width(16)) adder_1 (.a(A), .b(B), .out(adder_1_out), .cin(1'b0), .cout(adder_1_cout));
  Adder #(.width(16)) adder_2 (.a(A), .b(not_1_out), .out(adder_2_out), .cin(1'b1), .cout(adder_2_cout));
  assign and_1_out = A & B;  // AND_Gate and_1, 16 bits wide
  assign xor_1_out = A ^ B;  // XOR_Gate xor_1, 16 bits wide
  assign or_1_out = A | B;  // OR_Gate or_1, 16 bits wide
  Shifter #(.width(16)) shifter_1 (.in(A), .out(shifter_1_out));  // open: dist
  Shifter #(.shift("lr"), .width(16)) shifter_2 (.in(A), .out(shifter_2_out));  // open: dist
  Shifter #(.shift("ar"), .width(16)) shifter_3 (.in(A), .out(shifter_3_out));  // open: dist
  Multiplexer #(.select(3), .width(16)) multiplexer_1 (
    .in0(adder_1_out), .in1(adder_2_out), .in2(and_1_out), .in3(xor_1_out), .in4(or_1_out),
    .in5(shifter_1_out), .in6(shifter_2_out), .in7(shifter_3_out), .out(Result), .sel(Op));
  Multiplexer multiplexer_2 (.in0(adder_1_cout), .in1(adder_2_cout), .out(C), .sel(Op[0]));
  xor xor_2 (V, adder_1_cout, adder_2_cout);
  nor nor_1 (nor_1_out, undriven[0], undriven[1], undriven[2], undriven[3], undriven[4], undriven[5], undriven[6], undriven[7], undriven[8], undriven[9], undriven[10], undriven[11], undriven[12], undriven[13], undriven[14], N);
endmodule

module RegisterFile (
  input  [3:0] Rs2_Addr,
  input  [3:0] Rs1_Addr,
  input  [15:0] Write_data,
  input  clk,
  input  Reg_write,
  input  [3:0] Rd_addr,
  output [15:0] Rs2_data,
  output [15:0] Rs1_Data
);

  wire and_1_out, and_2_out, and_3_out, and_4_out, and_5_out, and_6_out, and_7_out, and_8_out, and_9_out,
       and_10_out, and_11_out, and_12_out, and_13_out, and_14_out, and_15_out, and_16_out, decoder_1_out0,
       decoder_1_out1, decoder_1_out2, decoder_1_out3, decoder_1_out4, decoder_1_out5, decoder_1_out6,
       decoder_1_out7, decoder_1_out8, decoder_1_out9, decoder_1_out10, decoder_1_out11, decoder_1_out12,
       decoder_1_out13, decoder_1_out14, decoder_1_out15;
  wire [15:0] R0_q, R1_q, R2_q, r3_q, R4_q, R5_q, R6_q, R7_q, R8_q, R9_q, R10_q, R11_q, R12_q, R13_q, R14_q,
       R15_q;

  Register #(.width(16)) R0 (.D(Write_data), .en(1'b0), .clk(clk), .Q(R0_q));  // open: clr
  and and_1 (and_1_out, decoder_1_out0, Reg_write);
  Register #(.width(16)) R1 (.D(Write_data), .en(and_2_out), .clk(clk), .Q(R1_q));  // open: clr
  and and_2 (and_2_out, decoder_1_out1, Reg_write);
  Register #(.width(16)) R2 (.D(Write_data), .en(and_3_out), .clk(clk), .Q(R2_q));  // open: clr
  and and_3 (and_3_out, decoder_1_out2, Reg_write);
  Register #(.width(16)) r3 (.D(Write_data), .en(and_4_out), .clk(clk), .Q(r3_q));  // open: clr
  and and_4 (and_4_out, decoder_1_out3, Reg_write);
  Register #(.width(16)) R4 (.D(Write_data), .en(and_5_out), .clk(clk), .Q(R4_q));  // open: clr
  and and_5 (and_5_out, decoder_1_out4, Reg_write);
  and and_6 (and_6_out, decoder_1_out5, Reg_write);
  Register #(.width(16)) R5 (.D(Write_data), .en(and_6_out), .clk(clk), .Q(R5_q));  // open: clr
  Decoder #(.enable("false"), .select(4)) decoder_1 (
    .out0(decoder_1_out0), .out1(decoder_1_out1), .out2(decoder_1_out2), .out3(decoder_1_out3),
    .out4(decoder_1_out4), .out5(decoder_1_out5), .out6(decoder_1_out6), .out7(decoder_1_out7),
    .out8(decoder_1_out8), .out9(decoder_1_out9), .out10(decoder_1_out10), .out11(decoder_1_out11),
    .out12(decoder_1_out12), .out13(decoder_1_out13), .out14(decoder_1_out14), .out15(decoder_1_out15),
    .sel(Rd_addr));
  Register #(.width(16)) R6 (.D(Write_data), .en(and_7_out), .clk(clk), .Q(R6_q));  // open: clr
  and and_7 (and_7_out, decoder_1_out6, Reg_write);
  Multiplexer #(.select(4), .width(16)) multiplexer_1 (
    .in0(R0_q), .in1(R1_q), .in2(R2_q), .in3(r3_q), .in4(R4_q), .in5(R5_q), .in6(R6_q), .in7(R7_q),
    .in8(R8_q), .in9(R9_q), .in10(R10_q), .in11(R11_q), .in12(R12_q), .in13(R13_q), .in14(R14_q),
    .in15(R15_q), .out(Rs1_Data), .sel(Rs1_Addr));
  Register #(.width(16)) R7 (.D(Write_data), .en(and_8_out), .clk(clk), .Q(R7_q));  // open: clr
  and and_8 (and_8_out, decoder_1_out7, Reg_write);
  Register #(.width(16)) R8 (.D(Write_data), .en(and_9_out), .clk(clk), .Q(R8_q));  // open: clr
  and and_9 (and_9_out, decoder_1_out8, Reg_write);
  Multiplexer #(.select(4), .width(16)) multiplexer_2 (
    .in0(R0_q), .in1(R1_q), .in2(R2_q), .in3(r3_q), .in4(R4_q), .in5(R5_q), .in6(R6_q), .in7(R7_q),
    .in8(R8_q), .in9(R9_q), .in10(R10_q), .in11(R11_q), .in12(R12_q), .in13(R13_q), .in14(R14_q),
    .in15(R15_q), .out(Rs2_data), .sel(Rs2_Addr));
  Register #(.width(16)) R9 (.D(Write_data), .en(and_10_out), .clk(clk), .Q(R9_q));  // open: clr
  and and_10 (and_10_out, decoder_1_out9, Reg_write);
  Register #(.width(16)) R10 (.D(Write_data), .en(and_11_out), .clk(clk), .Q(R10_q));  // open: clr
  and and_11 (and_11_out, decoder_1_out10, Reg_write);
  Register #(.width(16)) R11 (.D(Write_data), .en(and_12_out), .clk(clk), .Q(R11_q));  // open: clr
  and and_12 (and_12_out, decoder_1_out11, Reg_write);
  Register #(.width(16)) R12 (.D(Write_data), .en(and_13_out), .clk(clk), .Q(R12_q));  // open: clr
  and and_13 (and_13_out, decoder_1_out12, Reg_write);
  Register #(.width(16)) R13 (.D(Write_data), .en(and_14_out), .clk(clk), .Q(R13_q));  // open: clr
  and and_14 (and_14_out, decoder_1_out13, Reg_write);
  Register #(.width(16)) R14 (.D(Write_data), .en(and_15_out), .clk(clk), .Q(R14_q));  // open: clr
  and and_15 (and_15_out, decoder_1_out14, Reg_write);
  Register #(.width(16)) R15 (.D(Write_data), .en(and_16_out), .clk(clk), .Q(R15_q));  // open: clr
  and and_16 (and_16_out, decoder_1_out15, Reg_write);
endmodule

module PC (
  input  [15:0] BranchTarget,
  input  [15:0] jumptarget,
  input  jump,
  input  reset,
  input  branch,
  output [15:0] PC_out
);

  wire clock_1_out;
  wire [1:0] or_2_out;
  wire [15:0] adder_1_out, multiplexer_1_out;

  Register #(.width(16)) register_1 (.D(multiplexer_1_out), .en(1'b1), .clk(clock_1_out), .Q(PC_out));  // open: clr
  Clock clock_1 (.out(clock_1_out));
  Adder #(.width(16)) adder_1 (.a(PC_out), .b(16'h1), .out(adder_1_out));  // open: cin, cout
  or or_1 (or_2_out[1], jump, reset);
  Multiplexer #(.select(2), .width(16)) multiplexer_1 (
    .in0(adder_1_out), .in1(BranchTarget), .in2(jumptarget), .in3({16{1'b0}}), .out(multiplexer_1_out),
    .sel(or_2_out));
  or or_2 (or_2_out[0], reset, branch);
endmodule

module ControlUnit (
  input  [3:0] Opcode,
  output RegWrite,
  output MemRead,
  output MemWrite,
  output ALUSrc,
  output MemToReg,
  output Branch,
  output Jump,
  output [2:0] ALUOp
);

  wire and_1_out, and_4_out, and_5_out, and_7_out, and_8_out, and_12_out, and_13_out, and_14_out, not_1_out,
       not_2_out, not_3_out, not_4_out;

  not not_1 (not_1_out, Opcode[3]);
  not not_2 (not_2_out, Opcode[2]);
  not not_3 (not_3_out, Opcode[1]);
  not not_4 (not_4_out, Opcode[0]);
  and and_1 (and_1_out, not_2_out, not_3_out);
  and and_2 (MemRead, Opcode[3], not_2_out, not_3_out, Opcode[0]);
  and and_3 (MemWrite, Opcode[3], not_2_out, Opcode[1], not_4_out);
  and and_4 (and_4_out, Opcode[3], not_2_out, not_3_out);
  and and_5 (and_5_out, Opcode[3], not_2_out, not_4_out);
  and and_6 (MemToReg, Opcode[3], not_2_out, not_3_out, Opcode[0]);
  and and_7 (and_7_out, Opcode[3], not_2_out, Opcode[1], Opcode[0]);
  and and_8 (and_8_out, Opcode[3], Opcode[2], not_3_out, not_4_out);
  and and_9 (Jump, Opcode[3], Opcode[2], not_3_out, Opcode[0]);
  and and_10 (ALUOp[2], not_1_out, Opcode[2]);
  and and_11 (ALUOp[1], not_1_out, Opcode[1]);
  and and_12 (and_12_out, not_1_out, Opcode[0]);
  and and_13 (and_13_out, not_2_out, Opcode[1], Opcode[0]);
  and and_14 (and_14_out, Opcode[3], Opcode[2], not_3_out, not_4_out);
  or or_1 (RegWrite, not_1_out, and_1_out);
  or or_2 (ALUSrc, and_4_out, and_5_out);
  or or_3 (Branch, and_7_out, and_8_out);
  or or_4 (ALUOp[0], and_12_out, and_13_out, and_14_out);
endmodule
